# Fritzing sketch Sketch Projeto (saved by Fritzing 0.9.2b)
breadboards: 1

parts:
  Componente1 = Arduino Uno (Rev3)
  R1 = Rotary Potentiometer (Large) [maximum_resistance=100kΩ package=THT]
  U1 = POT [package=pot_alpha_rv16af-20]
  PIR1 = PIR sensor
  Tx1 = mystery part, 3 pins [chip_label=?]
  Rx1 = mystery part, 4 pins [chip_label=?]
  GY1 = GY-80

nets:
  N1: Componente1.A0, U1.S
  N2: Componente1.A1, R1.wiper
  N3: Componente1.A4/SDA, GY1.SDA
  N4: Componente1.A5/SCL, GY1.SCL
  GND: Componente1.GND, R1.leg2, U1.E, PIR1.GND, Tx1.pin3, Rx1.pin4, GY1.GND
  N5: Componente1.D2, Rx1.pin2
  N6: Componente1.D3_PWM, PIR1.SIG
  N7: Componente1.D4, Tx1.pin2
  5V: Componente1.5V, R1.leg1, U1.A, PIR1.VDD, Tx1.pin1, Rx1.pin1, GY1.VCC_IN

notes:
  Emissor RF
  Receptor RF

custom parts:
  GY-80: Placa GY-80 basada en conjunto de giroscopios L3G4200D + acelerómetros ADXL345 + magnetómetro HMC5883L + sensor barométrico BMP085
